# Fritzing sketch Sketch (saved by Fritzing 0.9.2b)
circuit board: 8.46667cm x 5.64444cm

parts:
  BT1 = Bluetooth HC-06u [package=THT]
  VCC2 = Battery
  Parte1 = Arduino Pro Mini v13
  VCC3 = Battery

nets:
  N1: BT1.VCC, VCC2.+
  N2: BT1.GND, VCC2.-
  N3: BT1.TXD, Parte1.D1/RX
  N4: BT1.RXD, Parte1.D0/TX
  N5: Parte1.VCC, VCC3.+
  N6: Parte1.GND, VCC3.-

custom parts:
  Bluetooth HC-06u: Bluetooth HC-06 - face up, pins down 16.5mm x 37.5mm PCB

// code stored in the sketch: Untitled.ino
void setup() {
Serial.begin(9600);

}

void loop(){
}
